// Logisim project RAMses.circ as structural Verilog
module deslocador (
  input  D1,
  input  D2,
  input  D3,
  input  D4,
  input  D5,
  input  D6,
  input  D7,
  input  D8,
  input  C,
  output out_10,
  output out_11,
  output out_12,
  output out_13,
  output out_14,
  output out_15,
  output out_16,
  output out_17
);

  wire and_1_out, and_3_out, and_4_out, and_5_out, and_6_out, and_7_out, and_8_out, and_9_out, and_10_out,
       and_11_out, and_12_out, and_14_out, not_1_out;

  and and_1 (and_1_out, D1, C);
  not not_1 (not_1_out, C);
  and and_2 (out_10, not_1_out, D2);
  and and_3 (and_3_out, D2, C);
  or or_1 (out_11, and_1_out, and_4_out);
  and and_4 (and_4_out, not_1_out, D3);
  or or_2 (out_12, and_3_out, and_7_out);
  and and_5 (and_5_out, D3, C);
  and and_6 (and_6_out, D4, C);
  and and_7 (and_7_out, not_1_out, D4);
  or or_3 (out_13, and_5_out, and_8_out);
  and and_8 (and_8_out, not_1_out, D5);
  and and_9 (and_9_out, D5, C);
  or or_4 (out_14, and_6_out, and_10_out);
  and and_10 (and_10_out, not_1_out, D6);
  and and_11 (and_11_out, D6, C);
  or or_5 (out_15, and_9_out, and_12_out);
  and and_12 (and_12_out, not_1_out, D7);
  or or_6 (out_16, and_11_out, and_14_out);
  and and_13 (out_17, D7, C);
  and and_14 (and_14_out, not_1_out, D8);
endmodule

// ULA(M)
module Unidade_Logica_Aritimetica_meio (
  input  A__inverter,
  input  A__habilitar,
  input  A,
  input  B,
  input  B__habilitar,
  input  F0,
  input  F1,
  input  F2,
  output Saida,
  output Vai_um
);

  wire and_1_out, and_2_out, and_3_out, complemento_de_2_completo_1_saida,
       complemento_de_2_completo_1_vai_um, decodificador3bits_1_d0, decodificador3bits_1_d1,
       decodificador3bits_1_d2, decodificador3bits_1_d3, decodificador3bits_1_d4, decodificador3bits_1_d5,
       decodificador3bits_1_d6, decodificador3bits_1_d7, deslocador_completo_1_saida,
       deslocador_completo_1_vai_um, somador_completo_1_resultado, somador_completo_1_vai_um,
       subtrador_completo_1_saida, subtrador_completo_1_vai_um, unidade_logica_1_and__saida,
       unidade_logica_1_not__saida, unidade_logica_1_or__saida, xor_1_out;

  and and_1 (and_1_out, A__habilitar, A);
  and and_2 (and_2_out, B, B__habilitar);
  Decodificador3Bits decodificador3bits_1 (
    .F0(F0), .F1(F1), .F2(F2), .D0(decodificador3bits_1_d0), .D1(decodificador3bits_1_d1),
    .D2(decodificador3bits_1_d2), .D3(decodificador3bits_1_d3), .D4(decodificador3bits_1_d4),
    .D5(decodificador3bits_1_d5), .D6(decodificador3bits_1_d6), .D7(decodificador3bits_1_d7));
  xor xor_1 (xor_1_out, A__inverter, and_1_out);
  and and_3 (and_3_out, and_2_out, decodificador3bits_1_d7);
  Unidade_Logica unidade_logica_1 (
    .A(xor_1_out), .B(and_2_out), .AND__habilita(decodificador3bits_1_d0),
    .OR__habilita(decodificador3bits_1_d1), .NOT__habilita(decodificador3bits_1_d2),
    .AND__saida(unidade_logica_1_and__saida), .OR__saida(unidade_logica_1_or__saida),
    .NOT__saida(unidade_logica_1_not__saida));
  Somador_Completo somador_completo_1 (
    .A(xor_1_out), .B(and_2_out), .Habilitar(decodificador3bits_1_d3), .Vem_um(1'b0),
    .Vai_Um(somador_completo_1_vai_um), .Resultado(somador_completo_1_resultado));
  Subtrador_Completo subtrador_completo_1 (
    .A(xor_1_out), .B(and_2_out), .Habilitar(decodificador3bits_1_d4), .Vem_um(1'b0),
    .Vai_um(subtrador_completo_1_vai_um), .Saida(subtrador_completo_1_saida));
  ExactlyOne xor_2 (
    .out(Vai_um), .in0(somador_completo_1_vai_um), .in1(subtrador_completo_1_vai_um),
    .in2(complemento_de_2_completo_1_vai_um), .in3(deslocador_completo_1_vai_um));
  Complemento_de_2_Completo complemento_de_2_completo_1 (
    .A(xor_1_out), .Vem_um(1'b1), .Habilitar(decodificador3bits_1_d5),
    .Vai_um(complemento_de_2_completo_1_vai_um), .Saida(complemento_de_2_completo_1_saida));
  Deslocador_Completo deslocador_completo_1 (
    .A(xor_1_out), .Vem_um(1'b0), .Habilitar(decodificador3bits_1_d6), .Vai_um(deslocador_completo_1_vai_um),
    .Saida(deslocador_completo_1_saida));
  ExactlyOne xor_3 (
    .out(Saida), .in0(unidade_logica_1_and__saida), .in1(unidade_logica_1_or__saida),
    .in2(unidade_logica_1_not__saida), .in3(and_3_out), .in4(somador_completo_1_resultado),
    .in5(subtrador_completo_1_saida), .in6(complemento_de_2_completo_1_saida),
    .in7(deslocador_completo_1_saida));
endmodule

// ULA
module Unidade_Logica_Aritimetica (
  input  Vem_um,
  input  A__inverter,
  input  A__habilitar,
  input  A,
  input  B,
  input  B__habilitar,
  input  F0,
  input  F1,
  input  F2,
  output Saida,
  output Vai_um
);

  wire and_1_out, and_2_out, and_3_out, complemento_de_2_completo_1_saida,
       complemento_de_2_completo_1_vai_um, decodificador3bits_1_d0, decodificador3bits_1_d1,
       decodificador3bits_1_d2, decodificador3bits_1_d3, decodificador3bits_1_d4, decodificador3bits_1_d5,
       decodificador3bits_1_d6, decodificador3bits_1_d7, deslocador_completo_1_saida,
       deslocador_completo_1_vai_um, somador_completo_1_resultado, somador_completo_1_vai_um,
       subtrador_completo_1_saida, subtrador_completo_1_vai_um, unidade_logica_1_and__saida,
       unidade_logica_1_not__saida, unidade_logica_1_or__saida, xor_1_out;

  and and_1 (and_1_out, A__habilitar, A);
  and and_2 (and_2_out, B, B__habilitar);
  Decodificador3Bits decodificador3bits_1 (
    .F0(F0), .F1(F1), .F2(F2), .D0(decodificador3bits_1_d0), .D1(decodificador3bits_1_d1),
    .D2(decodificador3bits_1_d2), .D3(decodificador3bits_1_d3), .D4(decodificador3bits_1_d4),
    .D5(decodificador3bits_1_d5), .D6(decodificador3bits_1_d6), .D7(decodificador3bits_1_d7));
  xor xor_1 (xor_1_out, A__inverter, and_1_out);
  and and_3 (and_3_out, and_2_out, decodificador3bits_1_d7);
  Unidade_Logica unidade_logica_1 (
    .A(xor_1_out), .B(and_2_out), .AND__habilita(decodificador3bits_1_d0),
    .OR__habilita(decodificador3bits_1_d1), .NOT__habilita(decodificador3bits_1_d2),
    .AND__saida(unidade_logica_1_and__saida), .OR__saida(unidade_logica_1_or__saida),
    .NOT__saida(unidade_logica_1_not__saida));
  Somador_Completo somador_completo_1 (
    .A(xor_1_out), .B(and_2_out), .Habilitar(decodificador3bits_1_d3), .Vem_um(Vem_um),
    .Vai_Um(somador_completo_1_vai_um), .Resultado(somador_completo_1_resultado));
  Subtrador_Completo subtrador_completo_1 (
    .A(xor_1_out), .B(and_2_out), .Habilitar(decodificador3bits_1_d4), .Vem_um(Vem_um),
    .Vai_um(subtrador_completo_1_vai_um), .Saida(subtrador_completo_1_saida));
  ExactlyOne xor_2 (
    .out(Vai_um), .in0(somador_completo_1_vai_um), .in1(subtrador_completo_1_vai_um),
    .in2(complemento_de_2_completo_1_vai_um), .in3(deslocador_completo_1_vai_um));
  Complemento_de_2_Completo complemento_de_2_completo_1 (
    .A(xor_1_out), .Vem_um(Vem_um), .Habilitar(decodificador3bits_1_d5),
    .Vai_um(complemento_de_2_completo_1_vai_um), .Saida(complemento_de_2_completo_1_saida));
  Deslocador_Completo deslocador_completo_1 (
    .A(xor_1_out), .Vem_um(Vem_um), .Habilitar(decodificador3bits_1_d6),
    .Vai_um(deslocador_completo_1_vai_um), .Saida(deslocador_completo_1_saida));
  ExactlyOne xor_3 (
    .out(Saida), .in0(unidade_logica_1_and__saida), .in1(unidade_logica_1_or__saida),
    .in2(unidade_logica_1_not__saida), .in3(and_3_out), .in4(somador_completo_1_resultado),
    .in5(subtrador_completo_1_saida), .in6(complemento_de_2_completo_1_saida),
    .in7(deslocador_completo_1_saida));
endmodule

module Unidade_Logica_Aritimetica_8bits (
  input  [7:0] A,
  input  [7:0] B,
  input  [2:0] \Funçao ,
  output [7:0] Saida
);

  wire unidade_logica_aritimetica_1_vai_um, unidade_logica_aritimetica_2_vai_um,
       unidade_logica_aritimetica_3_vai_um, unidade_logica_aritimetica_4_vai_um,
       unidade_logica_aritimetica_5_vai_um, unidade_logica_aritimetica_6_vai_um,
       unidade_logica_aritimetica_meio_1_vai_um;

  Unidade_Logica_Aritimetica_meio unidade_logica_aritimetica_meio_1 (
    .A__inverter(1'b0), .A__habilitar(1'b1), .A(A[0]), .B(B[0]), .B__habilitar(1'b1), .F0(\Funçao [0]),
    .F1(\Funçao [1]), .F2(\Funçao [2]), .Vai_um(unidade_logica_aritimetica_meio_1_vai_um), .Saida(Saida[0]));
  Unidade_Logica_Aritimetica unidade_logica_aritimetica_1 (
    .A__inverter(1'b0), .A__habilitar(1'b1), .A(A[1]), .B(B[1]), .B__habilitar(1'b1), .F0(\Funçao [0]),
    .F1(\Funçao [1]), .F2(\Funçao [2]), .Vem_um(unidade_logica_aritimetica_meio_1_vai_um),
    .Vai_um(unidade_logica_aritimetica_1_vai_um), .Saida(Saida[1]));
  Unidade_Logica_Aritimetica unidade_logica_aritimetica_2 (
    .A__inverter(1'b0), .A__habilitar(1'b1), .A(A[2]), .B(B[2]), .B__habilitar(1'b1), .F0(\Funçao [0]),
    .F1(\Funçao [1]), .F2(\Funçao [2]), .Vem_um(unidade_logica_aritimetica_1_vai_um),
    .Vai_um(unidade_logica_aritimetica_2_vai_um), .Saida(Saida[2]));
  Unidade_Logica_Aritimetica unidade_logica_aritimetica_3 (
    .A__inverter(1'b0), .A__habilitar(1'b1), .A(A[3]), .B(B[3]), .B__habilitar(1'b1), .F0(\Funçao [0]),
    .F1(\Funçao [1]), .F2(\Funçao [2]), .Vem_um(unidade_logica_aritimetica_2_vai_um),
    .Vai_um(unidade_logica_aritimetica_3_vai_um), .Saida(Saida[3]));
  Unidade_Logica_Aritimetica unidade_logica_aritimetica_4 (
    .A__inverter(1'b0), .A__habilitar(1'b1), .A(A[4]), .B(B[4]), .B__habilitar(1'b1), .F0(\Funçao [0]),
    .F1(\Funçao [1]), .F2(\Funçao [2]), .Vem_um(unidade_logica_aritimetica_3_vai_um),
    .Vai_um(unidade_logica_aritimetica_4_vai_um), .Saida(Saida[4]));
  Unidade_Logica_Aritimetica unidade_logica_aritimetica_5 (
    .A__inverter(1'b0), .A__habilitar(1'b1), .A(A[5]), .B(B[5]), .B__habilitar(1'b1), .F0(\Funçao [0]),
    .F1(\Funçao [1]), .F2(\Funçao [2]), .Vem_um(unidade_logica_aritimetica_4_vai_um),
    .Vai_um(unidade_logica_aritimetica_5_vai_um), .Saida(Saida[5]));
  Unidade_Logica_Aritimetica unidade_logica_aritimetica_6 (
    .A__inverter(1'b0), .A__habilitar(1'b1), .A(A[6]), .B(B[6]), .B__habilitar(1'b1), .F0(\Funçao [0]),
    .F1(\Funçao [1]), .F2(\Funçao [2]), .Vem_um(unidade_logica_aritimetica_5_vai_um),
    .Vai_um(unidade_logica_aritimetica_6_vai_um), .Saida(Saida[6]));
  Unidade_Logica_Aritimetica unidade_logica_aritimetica_7 (
    .A__inverter(1'b0), .A__habilitar(1'b1), .A(A[7]), .B(B[7]), .B__habilitar(1'b1), .F0(\Funçao [0]),
    .F1(\Funçao [1]), .F2(\Funçao [2]), .Vem_um(unidade_logica_aritimetica_6_vai_um), .Saida(Saida[7]));  // open: Vai_um
endmodule

// UL
module Unidade_Logica (
  input  A,
  input  B,
  input  AND__habilita,
  input  OR__habilita,
  input  NOT__habilita,
  output AND__saida,
  output OR__saida,
  output NOT__saida
);

  wire and_1_out, not_1_out, or_1_out;

  and and_1 (and_1_out, A, B);
  or or_1 (or_1_out, A, B);
  not not_1 (not_1_out, B);
  and and_2 (AND__saida, and_1_out, AND__habilita);
  and and_3 (OR__saida, or_1_out, OR__habilita);
  and and_4 (NOT__saida, not_1_out, NOT__habilita);
endmodule

// SUNCOM
module Somador_Completo (
  input  Vem_um,
  input  A,
  input  B,
  input  Habilitar,
  output Resultado,
  output Vai_Um
);

  wire and_1_out, and_2_out, xor_1_out, xor_2_out;

  and and_1 (and_1_out, Habilitar, B, A);
  xor xor_1 (xor_1_out, A, B);
  or or_1 (Vai_Um, and_1_out, and_2_out);
  and and_2 (and_2_out, Habilitar, xor_1_out, Vem_um);
  xor xor_2 (xor_2_out, Vem_um, xor_1_out);
  and and_3 (Resultado, xor_2_out, Habilitar);
endmodule

// SUBCOM
module Subtrador_Completo (
  input  Vem_um,
  input  A,
  input  B,
  input  Habilitar,
  output Saida,
  output Vai_um
);

  wire and_1_out, and_3_out, not_1_out, or_1_out, or_2_out, xor_1_out;

  not not_1 (not_1_out, A);
  and and_1 (and_1_out, not_1_out, or_1_out);
  and and_2 (Vai_um, Habilitar, or_2_out);
  or or_1 (or_1_out, B, Vem_um);
  or or_2 (or_2_out, and_1_out, and_3_out);
  xor xor_1 (xor_1_out, Vem_um, A, B);
  and and_3 (and_3_out, Vem_um, B, A);
  and and_4 (Saida, xor_1_out, Habilitar);
endmodule

// NEGCOM
module Complemento_de_2_Completo (
  input  Vem_um,
  input  A,
  input  Habilitar,
  output Saida,
  output Vai_um
);

  wire not_1_out, xor_1_out;

  not not_1 (not_1_out, A);
  and and_1 (Vai_um, not_1_out, Vem_um, Habilitar);
  xor xor_1 (xor_1_out, Vem_um, not_1_out);
  and and_2 (Saida, xor_1_out, Habilitar);
endmodule

// DESCOM
module Deslocador_Completo (
  input  Vem_um,
  input  A,
  input  Habilitar,
  output Saida,
  output Vai_um
);

  and and_1 (Vai_um, Habilitar, A);
  and and_2 (Saida, Vem_um, Habilitar);
endmodule

// DEC3B
module Decodificador3Bits (
  input  F0,
  input  F1,
  input  F2,
  output D0,
  output D1,
  output D2,
  output D3,
  output D4,
  output D5,
  output D6,
  output D7
);

  wire not_1_out, not_2_out, not_3_out, not_4_out, not_5_out, not_6_out, not_7_out, not_8_out, not_9_out,
       not_10_out, not_11_out, not_12_out;

  not not_1 (not_1_out, F0);
  not not_2 (not_2_out, F2);
  not not_3 (not_3_out, F1);
  not not_4 (not_4_out, F2);
  not not_5 (not_5_out, F1);
  not not_6 (not_6_out, F0);
  not not_7 (not_7_out, F2);
  not not_8 (not_8_out, F2);
  not not_9 (not_9_out, F1);
  not not_10 (not_10_out, F0);
  not not_11 (not_11_out, F1);
  not not_12 (not_12_out, F0);
  and and_1 (D0, not_1_out, not_2_out, not_3_out);
  and and_2 (D1, F0, not_4_out, not_5_out);
  and and_3 (D2, not_6_out, not_7_out, F1);
  and and_4 (D3, F1, not_8_out, F0);
  and and_5 (D4, not_9_out, F2, not_10_out);
  and and_6 (D5, not_11_out, F2, F0);
  and and_7 (D6, F1, F2, not_12_out);
  and and_8 (D7, F1, F2, F0);
endmodule

module ULA_in_8 (
  input  [7:0] A,
  input  [7:0] B,
  input  [2:0] Funcao
);

  wire [7:0] and_1_out;

  Decoder #(.select(3)) decoder_1 (.sel(Funcao), .en(1'b1));  // open: out0, out1, out2, out3, out4, out5, out6, out7
  assign and_1_out = A & B;  // AND_Gate and_1, 8 bits wide
endmodule

// FF-RSC
module flip_flop_R_S (
  input  Ativa,
  input  Reseta,
  output Saida
);

  wire nor_2_out;

  nor nor_1 (Saida, Reseta, nor_2_out);
  nor nor_2 (nor_2_out, Saida, Ativa);
endmodule

module registrador_8bits (
  input  [7:0] Entrada_de_Dados,
  input  Habilitar_Escrita,
  input  Resetar,
  input  Habilitar_Leitura,
  output [7:0] out_5
);

  wire and_1_out, and_2_out, and_4_out, and_6_out, and_8_out, and_10_out, and_12_out, and_14_out,
       flip_flop_r_s_1_saida, flip_flop_r_s_2_saida, flip_flop_r_s_3_saida, flip_flop_r_s_4_saida,
       flip_flop_r_s_5_saida, flip_flop_r_s_6_saida, flip_flop_r_s_7_saida, flip_flop_r_s_8_saida;

  and and_1 (and_1_out, Habilitar_Escrita, Entrada_de_Dados[7]);
  and and_2 (and_2_out, Habilitar_Escrita, Entrada_de_Dados[6]);
  flip_flop_R_S flip_flop_r_s_1 (.Ativa(and_1_out), .Reseta(Resetar), .Saida(flip_flop_r_s_1_saida));
  and and_3 (out_5[7], Habilitar_Leitura, flip_flop_r_s_1_saida);
  and and_4 (and_4_out, Habilitar_Escrita, Entrada_de_Dados[5]);
  flip_flop_R_S flip_flop_r_s_2 (.Ativa(and_2_out), .Reseta(Resetar), .Saida(flip_flop_r_s_2_saida));
  and and_5 (out_5[6], Habilitar_Leitura, flip_flop_r_s_2_saida);
  and and_6 (and_6_out, Habilitar_Escrita, Entrada_de_Dados[4]);
  flip_flop_R_S flip_flop_r_s_3 (.Ativa(and_4_out), .Reseta(Resetar), .Saida(flip_flop_r_s_3_saida));
  and and_7 (out_5[5], Habilitar_Leitura, flip_flop_r_s_3_saida);
  and and_8 (and_8_out, Habilitar_Escrita, Entrada_de_Dados[3]);
  flip_flop_R_S flip_flop_r_s_4 (.Ativa(and_6_out), .Reseta(Resetar), .Saida(flip_flop_r_s_4_saida));
  and and_9 (out_5[4], Habilitar_Leitura, flip_flop_r_s_4_saida);
  and and_10 (and_10_out, Habilitar_Escrita, Entrada_de_Dados[2]);
  flip_flop_R_S flip_flop_r_s_5 (.Ativa(and_8_out), .Reseta(Resetar), .Saida(flip_flop_r_s_5_saida));
  and and_11 (out_5[3], Habilitar_Leitura, flip_flop_r_s_5_saida);
  and and_12 (and_12_out, Habilitar_Escrita, Entrada_de_Dados[1]);
  flip_flop_R_S flip_flop_r_s_6 (.Ativa(and_10_out), .Reseta(Resetar), .Saida(flip_flop_r_s_6_saida));
  and and_13 (out_5[2], Habilitar_Leitura, flip_flop_r_s_6_saida);
  and and_14 (and_14_out, Habilitar_Escrita, Entrada_de_Dados[0]);
  flip_flop_R_S flip_flop_r_s_7 (.Ativa(and_12_out), .Reseta(Resetar), .Saida(flip_flop_r_s_7_saida));
  and and_15 (out_5[1], Habilitar_Leitura, flip_flop_r_s_7_saida);
  flip_flop_R_S flip_flop_r_s_8 (.Ativa(and_14_out), .Reseta(Resetar), .Saida(flip_flop_r_s_8_saida));
  and and_16 (out_5[0], Habilitar_Leitura, flip_flop_r_s_8_saida);
endmodule
